# Fritzing sketch 8-2 (saved by Fritzing 0.9.4)
breadboards: 1

parts:
  J1 = Basic Servo
  Part1 = Arduino Uno (Rev3)
  Part2 = Black Joystick KY-023

nets:
  GND: J1.gnd, Part1.GND, Part2.GND
  VCC: J1.vcc, Part1.5V, Part2.+5V
  N1: J1.pulse, Part1.D9_PWM
  N2: Part1.A0, Part2.VRx
  N3: Part1.A1, Part2.VRy
  N4: Part1.D2, Part2.SW

custom parts:
  Black Joystick KY-023: Description: The joystick is a combination of 2 analoog potentiometer and a digital switch. Arduino GND --> Module pin - Arduino +5V --> Module pin +5V Arduino Analoog 0 --> Module VRx Arduino Analoog 1 --> Module VRy Arduino Digital --> Module SW Dimensions: 1" x 1.25"
